# Fritzing sketch Untitled Sketch (saved by Fritzing 0.9.2b)
breadboards: 1

parts:
  Part1 = Arduino Nano (Rev3.0)
  R1 = Resistor [tolerance=±5% resistance=220 package=THT]
  R2 = Resistor [tolerance=±5% resistance=220 package=THT]
  R3 = Resistor [tolerance=±5% resistance=220 package=THT]
  R4 = Resistor [tolerance=±5% resistance=220 package=THT]
  R5 = Resistor [tolerance=±5% resistance=220 package=THT]
  LED1 = LED - 5mm [color="Red (633nm)" package="5 mm [THT]"]
  LED2 = LED - 5mm [color="Red (633nm)" package="5 mm [THT]"]
  LED3 = LED - 5mm [color="Red (633nm)" package="5 mm [THT]"]
  LED4 = LED - 5mm [color="Red (633nm)" package="5 mm [THT]"]
  LED5 = LED - 5mm [color="Red (633nm)" package="5 mm [THT]"]
  VCC1 = Battery block 9V

nets:
  N1: Part1.GND, R1.Pin_1, R2.Pin_1, R3.Pin_1, R4.Pin_1, R5.Pin_1, VCC1.-
  N2: Part1.D4, LED1.anode
  N3: Part1.D5, LED2.anode
  N4: Part1.D6, LED3.anode
  N5: Part1.D7, LED4.anode
  N6: Part1.D8, LED5.anode
  N7: Part1.VIN, VCC1.+
  N8: R1.Pin_0, LED3.cathode
  N9: R2.Pin_0, LED4.cathode
  N10: R3.Pin_0, LED2.cathode
  N11: R4.Pin_0, LED1.cathode
  N12: R5.Pin_0, LED5.cathode
