# Fritzing sketch schema (saved by Fritzing 0.9.2b)
breadboards: 1

parts:
  Part1 = Arduino Nano (Rev3.0)
  LED1 = LED - 5mm [color="Red (633nm)" package="5 mm [THT]"]
  LED2 = LED - 5mm [color="Red (633nm)" package="5 mm [THT]"]
  LED3 = LED - 5mm [color="Red (633nm)" package="5 mm [THT]"]
  LED4 = LED - 5mm [color="Red (633nm)" package="5 mm [THT]"]
  LED5 = LED - 5mm [color="Red (633nm)" package="5 mm [THT]"]
  R1 = Resistor [tolerance=±5% resistance=220 package=THT]
  R2 = Resistor [tolerance=±5% resistance=220 package=THT]
  R3 = Resistor [tolerance=±5% resistance=220 package=THT]
  R4 = Resistor [tolerance=±5% resistance=220 package=THT]
  R5 = Resistor [tolerance=±5% resistance=220 package=THT]
  VCC1 = Battery block 9V

nets (from the breadboard view):
  N1: Part1.GND, R1.Pin_1, R2.Pin_1, R3.Pin_1, R5.Pin_1, VCC1.-
  N2: Part1.D4, LED1.cathode
  N3: Part1.D5, LED2.cathode
  N4: Part1.D6, LED3.cathode
  N5: Part1.D7, LED4.cathode
  N6: Part1.D8, LED5.cathode
  N7: Part1.VIN, VCC1.+
  N8: LED1.anode, R1.Pin_0
  N9: LED2.anode, R2.Pin_0
  N10: LED3.anode, R3.Pin_0
  N11: LED4.anode, R4.Pin_0
  N12: LED5.anode, R5.Pin_0

// code stored in the sketch: lightshow-rubix-kidshackathon.ino
/*
  Rubix kids Hackathon, let 5 LED burn in different sequences
  
  bvo
*/


// the setup function runs once when you press reset or power the board
void setup() {
  // initialize digital pins 4,...,8 as an output.
  for (int i=4;i<9; i = i + 1) {
    pinMode(i, OUTPUT);
  }
}



// the loop function runs over and over again forever
void loop() {
  
  
  for (int j=1;j<3;j=j+1){
    
    // All LED together
    //
    for (int i=4;i<9; i = i + 1) {
      digitalWrite(i, HIGH);
    }
    delay(1000);
    for (int i=4;i<9; i = i + 1) {
      digitalWrite(i, LOW);
    }
    delay(1000);
    
  }
  delay(1000);
  
  // Per LED on/off forward
  //
  for (int i=4;i<9; i = i + 1) {
     digitalWrite(i, HIGH);
     delay(250);
     digitalWrite(i, LOW);
     delay(250);
  }
  delay(1000);
  
  // Per LED on/off backward
  //
  for (int i=9;i>3; i = i - 1) {
     digitalWrite(i, HIGH);
     delay(250);
     digitalWrite(i, LOW);
     delay(250);
  }
  delay(1000);
  
  // repeat twice
  //
  for (int j=1;j<3;j=j+1){
  
  // Per LED starting in middle to edge
  //
  for (int i=0;i<4; i = i + 1) {
     int af = 6 + i;
     int op = 6 - i;
     digitalWrite(af, HIGH);
     digitalWrite(op, HIGH);
     delay(250);
     digitalWrite(af, LOW);
     digitalWrite(op, LOW);
     delay(250);
  }
  delay(1000);
  
  // Per LED starting in edges to middle
  //
  for (int i=0;i<3; i = i + 1) {
     int af = 4 + i;
     int op = 8 - i;
     digitalWrite(af, HIGH);
     digitalWrite(op, HIGH);
     delay(250);
     digitalWrite(af, LOW);
     digitalWrite(op, LOW);
     delay(250);
  }
  delay(1000);
  
  }
  delay(1000);
  
}
